// Logisim project AoEProject.circ as structural Verilog: 10 circuits, main circuit 8bitALUwBuses
module CPU (
  input  [2:0] in_1,
  input  [2:0] in_2
);

  wire and_1_out, and_2_out, and_3_out, and_4_out, and_5_out, and_6_out, and_7_out, and_8_out, clock_1_out,
       not_1_out, not_2_out, not_3_out, not_4_out, not_5_out, not_6_out, not_7_out, not_8_out, not_9_out,
       not_10_out, not_11_out, or_1_out;
  wire [2:0] multiplexer_3_out;
  wire [3:0] multiplexer_2_out;
  wire [7:0] counter_1_q, extender_1_out_2, extender_2_out_2, multiplexer_1_out, multiplexer_4_out,
       multiplexer_5_out, n8bitaluwbuses_1_out_4, n8bitaluwbuses_2_out_4, ram_1_data, registerfile_1_rs1out,
       registerfile_1_rs2out, xnor_1_out;
  wire [15:0] rom_1_data;

  Multiplexer #(.width(8)) multiplexer_1 (
    .in0(counter_1_q), .in1(n8bitaluwbuses_1_out_4), .out(multiplexer_1_out), .sel(and_1_out));  // open: en
  _8bitALUwBuses u_8bitaluwbuses_1 (
    .IN1(counter_1_q), .IN2(extender_1_out_2), .OPCODE(in_1), .out_4(n8bitaluwbuses_1_out_4));
  and and_1 (and_1_out, and_2_out, and_3_out);
  Counter counter_1 (.D(multiplexer_1_out), .Q(counter_1_q), .clk(clock_1_out));  // open: load, count, carry, clr
  and and_2 (and_2_out, not_1_out, not_2_out, rom_1_data[2]);
  not not_1 (not_1_out, rom_1_data[0]);
  not not_2 (not_2_out, rom_1_data[1]);
  extender extender_1 (.in_1(rom_1_data[7:4]), .out_2(extender_1_out_2));
  ROM #(.dataWidth(16)) rom_1 (.addr(counter_1_q), .data(rom_1_data));  // open: sel
  Clock clock_1 (.out(clock_1_out));
  and and_3 (and_3_out, xnor_1_out[0], xnor_1_out[1], xnor_1_out[2], xnor_1_out[3], xnor_1_out[4], xnor_1_out[5], xnor_1_out[6], xnor_1_out[7]);
  not not_3 (not_3_out, rom_1_data[1]);
  not not_4 (not_4_out, rom_1_data[2]);
  not not_5 (not_5_out, rom_1_data[0]);
  Multiplexer #(.width(4)) multiplexer_2 (
    .in0(rom_1_data[15:12]), .in1(rom_1_data[7:4]), .out(multiplexer_2_out), .sel(rom_1_data[0]));  // open: en
  and and_4 (and_4_out, rom_1_data[0], not_3_out, not_4_out);
  and and_5 (and_5_out, not_5_out, rom_1_data[1], rom_1_data[2]);
  assign xnor_1_out = ~(registerfile_1_rs2out ^ registerfile_1_rs1out);  // XNOR_Gate xnor_1, 8 bits wide
  not not_6 (not_6_out, or_1_out);
  or or_1 (or_1_out, and_4_out, and_5_out);
  extender extender_2 (.in_1(multiplexer_2_out), .out_2(extender_2_out_2));
  RegisterFile registerfile_1 (
    .ClockIN(clock_1_out), .MemIN(multiplexer_5_out), .WRITE(not_6_out), .rd(rom_1_data[7:4]),
    .rs1(rom_1_data[11:8]), .rs2(rom_1_data[15:12]), .rs1OUT(registerfile_1_rs1out),
    .rs2OUT(registerfile_1_rs2out));
  Multiplexer #(.width(3)) multiplexer_3 (
    .in0(rom_1_data[2:0]), .in1(in_2), .out(multiplexer_3_out), .sel(not_7_out));  // open: en
  not not_7 (not_7_out, rom_1_data[2]);
  Multiplexer #(.width(8)) multiplexer_4 (
    .in0(registerfile_1_rs2out), .in1(extender_2_out_2), .out(multiplexer_4_out), .sel(and_6_out));  // open: en
  and and_6 (and_6_out, not_8_out, rom_1_data[1]);
  not not_8 (not_8_out, rom_1_data[2]);
  _8bitALUwBuses u_8bitaluwbuses_2 (
    .IN1(registerfile_1_rs1out), .IN2(multiplexer_4_out), .OPCODE(multiplexer_3_out),
    .out_4(n8bitaluwbuses_2_out_4));
  and and_7 (and_7_out, not_9_out, rom_1_data[1], rom_1_data[0]);
  not not_9 (not_9_out, rom_1_data[2]);
  RAM #(.bus("separate")) ram_1 (
    .addr(n8bitaluwbuses_2_out_4), .din(registerfile_1_rs2out), .data(ram_1_data), .str(and_7_out),
    .clk(clock_1_out), .ld(and_8_out));  // open: sel, clr
  not not_10 (not_10_out, rom_1_data[2]);
  Multiplexer #(.width(8)) multiplexer_5 (
    .in0(n8bitaluwbuses_2_out_4), .in1(ram_1_data), .out(multiplexer_5_out), .sel(and_8_out));  // open: en
  and and_8 (and_8_out, not_10_out, rom_1_data[1], not_11_out);
  not not_11 (not_11_out, rom_1_data[0]);

  // Notes on the sheet:
  //   extender
  //   instruction memory
  //   contents of rom_1 (hex, n*v repeats v):
  //   2 4 703 2 4 703 2 4 703
  //   extender
  //   register
  //   alu
  //   data memory
endmodule

module RegisterFile (
  input  ClockIN,
  input  [7:0] MemIN,
  input  [3:0] rs1,
  input  WRITE,
  input  [3:0] rd,
  input  [3:0] rs2,
  output [7:0] rs1OUT,
  output [7:0] rs2OUT
);

  wire demultiplexer_2_out0, demultiplexer_2_out1, demultiplexer_2_out2, demultiplexer_2_out3,
       demultiplexer_2_out4, demultiplexer_2_out5, demultiplexer_2_out6, demultiplexer_2_out7,
       demultiplexer_2_out8, demultiplexer_2_out9, demultiplexer_2_out10, demultiplexer_2_out11,
       demultiplexer_2_out12, demultiplexer_2_out13, demultiplexer_2_out14, demultiplexer_2_out15;
  wire [7:0] demultiplexer_1_out0, demultiplexer_1_out1, demultiplexer_1_out2, demultiplexer_1_out3,
       demultiplexer_1_out4, demultiplexer_1_out5, demultiplexer_1_out6, demultiplexer_1_out7,
       demultiplexer_1_out8, demultiplexer_1_out9, demultiplexer_1_out10, demultiplexer_1_out11,
       demultiplexer_1_out12, demultiplexer_1_out13, demultiplexer_1_out14, demultiplexer_1_out15,
       register_1_q, register_2_q, register_3_q, register_4_q, register_5_q, register_6_q, register_7_q,
       register_8_q, register_9_q, register_10_q, register_11_q, register_12_q, register_13_q, register_14_q,
       register_15_q, register_16_q;

  Demultiplexer #(.select(4), .width(8)) demultiplexer_1 (
    .out0(demultiplexer_1_out0), .out1(demultiplexer_1_out1), .out2(demultiplexer_1_out2),
    .out3(demultiplexer_1_out3), .out4(demultiplexer_1_out4), .out5(demultiplexer_1_out5),
    .out6(demultiplexer_1_out6), .out7(demultiplexer_1_out7), .out8(demultiplexer_1_out8),
    .out9(demultiplexer_1_out9), .out10(demultiplexer_1_out10), .out11(demultiplexer_1_out11),
    .out12(demultiplexer_1_out12), .out13(demultiplexer_1_out13), .out14(demultiplexer_1_out14),
    .out15(demultiplexer_1_out15), .in(MemIN), .sel(rd), .en(1'b1));
  Demultiplexer #(.select(4)) demultiplexer_2 (
    .out0(demultiplexer_2_out0), .out1(demultiplexer_2_out1), .out2(demultiplexer_2_out2),
    .out3(demultiplexer_2_out3), .out4(demultiplexer_2_out4), .out5(demultiplexer_2_out5),
    .out6(demultiplexer_2_out6), .out7(demultiplexer_2_out7), .out8(demultiplexer_2_out8),
    .out9(demultiplexer_2_out9), .out10(demultiplexer_2_out10), .out11(demultiplexer_2_out11),
    .out12(demultiplexer_2_out12), .out13(demultiplexer_2_out13), .out14(demultiplexer_2_out14),
    .out15(demultiplexer_2_out15), .in(WRITE), .sel(rd), .en(1'b1));
  Register register_1 (
    .D(demultiplexer_1_out0), .en(demultiplexer_2_out0), .Q(register_1_q), .clk(ClockIN));  // open: clr
  Register register_2 (
    .D(demultiplexer_1_out1), .en(demultiplexer_2_out1), .Q(register_2_q), .clk(ClockIN));  // open: clr
  Register register_3 (
    .D(demultiplexer_1_out2), .en(demultiplexer_2_out2), .Q(register_3_q), .clk(ClockIN));  // open: clr
  Register register_4 (
    .D(demultiplexer_1_out3), .en(demultiplexer_2_out3), .Q(register_4_q), .clk(ClockIN));  // open: clr
  Register register_5 (
    .D(demultiplexer_1_out4), .en(demultiplexer_2_out4), .Q(register_5_q), .clk(ClockIN));  // open: clr
  Register register_6 (
    .D(demultiplexer_1_out5), .en(demultiplexer_2_out5), .Q(register_6_q), .clk(ClockIN));  // open: clr
  Register register_7 (
    .D(demultiplexer_1_out6), .en(demultiplexer_2_out6), .Q(register_7_q), .clk(ClockIN));  // open: clr
  Register register_8 (
    .D(demultiplexer_1_out7), .en(demultiplexer_2_out7), .Q(register_8_q), .clk(ClockIN));  // open: clr
  Register register_9 (
    .D(demultiplexer_1_out8), .en(demultiplexer_2_out8), .Q(register_9_q), .clk(ClockIN));  // open: clr
  Register register_10 (
    .D(demultiplexer_1_out9), .en(demultiplexer_2_out9), .Q(register_10_q), .clk(ClockIN));  // open: clr
  Register register_11 (
    .D(demultiplexer_1_out10), .en(demultiplexer_2_out10), .Q(register_11_q), .clk(ClockIN));  // open: clr
  Register register_12 (
    .D(demultiplexer_1_out11), .en(demultiplexer_2_out11), .Q(register_12_q), .clk(ClockIN));  // open: clr
  Register register_13 (
    .D(demultiplexer_1_out12), .en(demultiplexer_2_out12), .Q(register_13_q), .clk(ClockIN));  // open: clr
  Register register_14 (
    .D(demultiplexer_1_out13), .en(demultiplexer_2_out13), .Q(register_14_q), .clk(ClockIN));  // open: clr
  Register register_15 (
    .D(demultiplexer_1_out14), .en(demultiplexer_2_out14), .Q(register_15_q), .clk(ClockIN));  // open: clr
  Register register_16 (
    .D(demultiplexer_1_out15), .en(demultiplexer_2_out15), .Q(register_16_q), .clk(ClockIN));  // open: clr
  Multiplexer #(.select(4), .width(8)) multiplexer_1 (
    .in0(register_1_q), .in1(register_2_q), .in2(register_3_q), .in3(register_4_q), .in4(register_5_q),
    .in5(register_6_q), .in6(register_7_q), .in7(register_8_q), .in8(register_9_q), .in9(register_10_q),
    .in10(register_11_q), .in11(register_12_q), .in12(register_13_q), .in13(register_14_q),
    .in14(register_15_q), .in15(register_16_q), .out(rs1OUT), .sel(rs1), .en(1'b1));
  Multiplexer #(.select(4), .width(8)) multiplexer_2 (
    .in0(register_1_q), .in1(register_2_q), .in2(register_3_q), .in3(register_4_q), .in4(register_5_q),
    .in5(register_6_q), .in6(register_7_q), .in7(register_8_q), .in8(register_9_q), .in9(register_10_q),
    .in10(register_11_q), .in11(register_12_q), .in12(register_13_q), .in13(register_14_q),
    .in14(register_15_q), .in15(register_16_q), .out(rs2OUT), .sel(rs2), .en(1'b1));
endmodule

module _8BitALU (
  input  InBit1,
  input  in_2,
  input  in_3,
  input  in_4,
  input  in_5,
  input  in_6,
  input  in_7,
  input  in_8,
  input  in_9,
  input  in_10,
  input  in_11,
  input  in_12,
  input  in_13,
  input  in_14,
  input  in_15,
  input  in_16,
  input  [1:0] in_17,
  input  in_18,
  output out_19,
  output out_20,
  output out_21,
  output out_22,
  output out_23,
  output out_24,
  output out_25,
  output out_26
);

  wire onebitalu_1_out_5, onebitalu_2_out_5, onebitalu_3_out_5, onebitalu_4_out_5, onebitalu_5_out_5,
       onebitalu_6_out_5, onebitalu_7_out_5;

  OneBitALU onebitalu_1 (
    .CIN(in_18), .IN1(InBit1), .IN2(in_9), .in_4(in_17), .out_5(onebitalu_1_out_5), .out_6(out_19));
  OneBitALU onebitalu_2 (
    .CIN(onebitalu_1_out_5), .IN1(in_2), .IN2(in_10), .in_4(in_17), .out_5(onebitalu_2_out_5), .out_6(out_20));
  OneBitALU onebitalu_3 (
    .CIN(onebitalu_2_out_5), .IN1(in_3), .IN2(in_11), .in_4(in_17), .out_5(onebitalu_3_out_5), .out_6(out_21));
  OneBitALU onebitalu_4 (
    .CIN(onebitalu_3_out_5), .IN1(in_4), .IN2(in_12), .in_4(in_17), .out_5(onebitalu_4_out_5), .out_6(out_22));
  OneBitALU onebitalu_5 (
    .CIN(onebitalu_4_out_5), .IN1(in_5), .IN2(in_13), .in_4(in_17), .out_5(onebitalu_5_out_5), .out_6(out_23));
  OneBitALU onebitalu_6 (
    .CIN(onebitalu_5_out_5), .IN1(in_6), .IN2(in_14), .in_4(in_17), .out_5(onebitalu_6_out_5), .out_6(out_24));
  OneBitALU onebitalu_7 (
    .CIN(onebitalu_6_out_5), .IN1(in_7), .IN2(in_15), .in_4(in_17), .out_5(onebitalu_7_out_5), .out_6(out_25));
  OneBitALU onebitalu_8 (
    .CIN(onebitalu_7_out_5), .IN1(in_8), .IN2(in_16), .in_4(in_17), .out_6(out_26));  // open: out_5
endmodule

module _8bitALUwBuses (
  input  [7:0] IN1,
  input  [7:0] IN2,
  input  [2:0] OPCODE,
  output [7:0] out_4
);

  wire not_1_out;

  _8BitALU u_8bitalu_1 (
    .InBit1(IN1[0]), .in_2(IN1[1]), .in_3(IN1[2]), .in_4(IN1[3]), .in_5(IN1[4]), .in_6(IN1[5]),
    .in_7(IN1[6]), .in_8(IN1[7]), .in_9(IN2[0]), .in_10(IN2[1]), .in_11(IN2[2]), .in_12(IN2[3]),
    .in_13(IN2[4]), .in_14(IN2[5]), .in_15(IN2[6]), .in_16(IN2[7]), .in_17(OPCODE[1:0]), .in_18(not_1_out),
    .out_19(out_4[0]), .out_20(out_4[1]), .out_21(out_4[2]), .out_22(out_4[3]), .out_23(out_4[4]),
    .out_24(out_4[5]), .out_25(out_4[6]), .out_26(out_4[7]));
  not not_1 (not_1_out, 1'b1);
endmodule

module OneBitAdder (
  input  Carry_In,
  input  First_Bit,
  input  Second_Bit,
  output SUM,
  output Carry_Out
);

  wire and_1_out, and_2_out, and_3_out, and_4_out, and_5_out, and_6_out, and_7_out, not_1_out, not_2_out,
       not_3_out, not_4_out, or_1_out;

  not not_1 (not_1_out, First_Bit);
  and and_1 (and_1_out, not_1_out, Second_Bit);
  and and_2 (and_2_out, First_Bit, not_2_out);
  not not_2 (not_2_out, Second_Bit);
  or or_1 (or_1_out, and_1_out, and_2_out);
  not not_3 (not_3_out, Carry_In);
  and and_3 (and_3_out, not_3_out, or_1_out);
  and and_4 (and_4_out, Carry_In, not_4_out);
  not not_4 (not_4_out, or_1_out);
  and and_5 (and_5_out, First_Bit, Carry_In);
  and and_6 (and_6_out, Carry_In, Second_Bit);
  and and_7 (and_7_out, First_Bit, Second_Bit);
  or or_2 (SUM, and_3_out, and_4_out);
  or or_3 (Carry_Out, and_5_out, and_6_out, and_7_out);

  // Notes on the sheet:
  //   One Bit Adder
endmodule

module OneBitALU (
  input  CIN,
  input  IN1,
  input  IN2,
  input  [1:0] in_4,
  output out_5,
  output out_6
);

  wire and_1_out, onebitadder_1_sum, or_1_out;

  OneBitAdder onebitadder_1 (
    .Carry_In(IN2), .First_Bit(IN1), .Second_Bit(CIN), .SUM(onebitadder_1_sum), .Carry_Out(out_5));
  and and_1 (and_1_out, IN1, IN2);
  or or_1 (or_1_out, IN1, IN2);
  Multiplexer #(.select(2), .enable("false")) multiplexer_1 (
    .in0(onebitadder_1_sum), .in2(and_1_out), .in3(or_1_out), .out(out_6), .sel(in_4));  // open: in1
endmodule

module extender (
  input  [3:0] in_1,
  output [7:0] out_2
);

  not not_1 (out_2[4], 1'b1);
  not not_2 (out_2[5], 1'b1);
  not not_3 (out_2[6], 1'b1);
  not not_4 (out_2[7], 1'b1);

  assign out_2[3:0] = in_1;
endmodule

module test1 (
  input  [3:0] in_1,
  input  in_2,
  output [7:0] out_3
);

  wire clock_1_out;
  wire [3:0] demultiplexer_1_out4, demultiplexer_2_out4, demultiplexer_3_out4;
  wire [7:0] counter_1_q, n8bitaluwbuses_1_out_4, registerfile_1_rs1out, registerfile_1_rs2out;
  wire [15:0] ram_1_data;

  Counter counter_1 (.Q(counter_1_q), .clk(clock_1_out));  // open: load, D, count, carry, clr
  Clock clock_1 (.out(clock_1_out));
  RAM #(.dataWidth(16)) ram_1 (.addr(counter_1_q), .data(ram_1_data));  // open: sel, clk, ld, clr
  Demultiplexer #(.select(3), .width(4)) demultiplexer_1 (
    .out4(demultiplexer_1_out4), .out6(demultiplexer_1_out4), .out7(demultiplexer_1_out4),
    .in(ram_1_data[7:4]), .sel(ram_1_data[2:0]));  // open: out0, out1, out2, out3, out5, en
  Demultiplexer #(.select(3), .width(4)) demultiplexer_2 (
    .out4(demultiplexer_2_out4), .out6(demultiplexer_2_out4), .out7(demultiplexer_2_out4),
    .in(ram_1_data[11:8]), .sel(ram_1_data[2:0]));  // open: out0, out1, out2, out3, out5, en
  Demultiplexer #(.select(3), .width(4)) demultiplexer_3 (
    .out4(demultiplexer_3_out4), .out6(demultiplexer_3_out4), .out7(demultiplexer_3_out4),
    .in(ram_1_data[15:12]), .sel(ram_1_data[2:0]));  // open: out0, out1, out2, out3, out5, en
  not not_1 (out_3[4], 1'b1);
  not not_2 (out_3[5], 1'b1);
  not not_3 (out_3[6], 1'b1);
  not not_4 (out_3[7], 1'b1);
  RegisterFile registerfile_1 (
    .ClockIN(clock_1_out), .MemIN(n8bitaluwbuses_1_out_4), .WRITE(in_2), .rd(demultiplexer_1_out4),
    .rs1(demultiplexer_3_out4), .rs2(demultiplexer_2_out4), .rs1OUT(registerfile_1_rs1out),
    .rs2OUT(registerfile_1_rs2out));
  RAM ram_2 ();  // open: addr, data, sel, clk, ld, clr
  _8bitALUwBuses u_8bitaluwbuses_1 (
    .IN1(registerfile_1_rs1out), .IN2(registerfile_1_rs2out), .OPCODE(ram_1_data[2:0]),
    .out_4(n8bitaluwbuses_1_out_4));

  assign out_3[3:0] = in_1;

  // Notes on the sheet:
  //   2: ld
  //   3:store
  //   4:add
  //   0: noop
  //   1: branch
  //   instruction memory
  //   5:subtract
  //   6: and
  //   7:or
  //   register
  //   data memory
  //   alu
endmodule

module test2 (
  input  [7:0] in_1,
  input  [3:0] in_2,
  input  [3:0] in_3,
  input  [2:0] in_4,
  input  [3:0] in_5,
  output [7:0] out_6
);

  wire clock_1_out;
  wire [3:0] counter_1_q;
  wire [7:0] undriven, undriven_2;
  wire [15:0] ram_1_data;

  Clock clock_1 (.out(clock_1_out));
  Counter #(.width(4), .max('hf)) counter_1 (.Q(counter_1_q), .clk(clock_1_out));  // open: load, D, count, carry, clr
  RAM #(.addrWidth(4), .dataWidth(16)) ram_1 (
    .addr(counter_1_q), .data(ram_1_data), .clk(clock_1_out));  // open: sel, ld, clr
  _8bitALUwBuses u_8bitaluwbuses_1 (.IN1(undriven), .IN2(undriven_2), .OPCODE(in_4), .out_4(out_6));
  RAM ram_2 ();  // open: addr, data, sel, clk, ld, clr

  // Notes on the sheet:
  //   Instruction memory
  //   data memory
endmodule

module test (
  input  [3:0] INPUT,
  input  ENABLED,
  input  in_3,
  input  [7:0] in_4,
  input  in_5,
  input  STORE,
  input  LOAD,
  input  [7:0] INPUT_B,
  input  [1:0] in_9,
  input  [7:0] in_10,
  input  in_11,
  output [7:0] out_12,
  output [7:0] out_13
);

  wire clock_1_out;
  wire [2:0] undriven;
  wire [3:0] register_1_q;
  wire [7:0] multiplexer_1_out, ram_2_data, register_2_q;

  Counter counter_1 ();  // open: load, D, count, Q, carry, clk, clr
  RAM #(.addrWidth(5), .dataWidth(16)) ram_1 ();  // open: addr, data, sel, clk, ld, clr
  _8bitALUwBuses u_8bitaluwbuses_1 (.IN1(in_10), .IN2(multiplexer_1_out), .OPCODE(undriven), .out_4(out_13));
  Clock clock_1 (.out(clock_1_out));
  Multiplexer #(.select(2), .width(8)) multiplexer_1 (
    .in0(INPUT_B), .out(multiplexer_1_out), .sel(in_9));  // open: in1, in2, in3, en
  Register #(.width(4)) register_1 (.D(INPUT), .en(ENABLED), .Q(register_1_q), .clk(clock_1_out));  // open: clr
  Register register_2 (.D(in_4), .en(in_5), .Q(register_2_q), .clk(clock_1_out));  // open: clr
  Demultiplexer #(.select(2)) demultiplexer_1 ();  // open: out0, out1, out2, out3, in, sel, en
  RAM #(.addrWidth(4), .bus("separate")) ram_2 (
    .addr(register_1_q), .din(register_2_q), .data(ram_2_data), .str(STORE), .ld(LOAD));  // open: sel, clk, clr
  Multiplexer #(.select(2)) multiplexer_2 ();  // open: in0, in1, in2, in3, out, sel, en
  Register register_3 (.D(ram_2_data), .en(in_3), .clk(clock_1_out));  // open: Q, clr

  // Notes on the sheet:
  //   16 different registers in a seperate file
  //   INSTRUCTION MEMORY
  //   CONTROL SIGNAL FOR MUX
  //   program counter that increases whenever the clock goes
  //   OUT
  //   INPUT A
  //   REGISTER
  //   CLOCK
  //   CONTROL SIGNAL FOR ALU
  //   DATA MEMORY
  //   use a second mux to tell me whether it is a memory instruction
  //   OUTPUT FROM MEMORY
endmodule
